// Logisim project cpu.circ as structural Verilog: 1 circuit, main circuit main
module main (
  input  [31:0] INSTRUCTION,
  input  CLOCK,
  output [31:0] PROGRAM_COUNTER,
  output [31:0] ra,
  output [31:0] sp,
  output [31:0] t0,
  output [31:0] t1,
  output [31:0] t2,
  output [31:0] s0,
  output [31:0] s1,
  output [31:0] a0
);

  wire [2:0] funct3;
  wire [11:0] imm;
  wire [19:0] INSTRUCTION_AfterReg;
  wire [31:0] adder_1_out, ALU_output, DMEM_ReadData, immediate, PC_AfterReg, rs1_output, WBValue;

  // control_logic control_logic_1: pin names not known
  Adder #(.width(32)) adder_1 (.a(PROGRAM_COUNTER), .b(32'h4), .out(adder_1_out));  // open: cin, cout
  Register #(.width(32)) register_1 (
    .D(INSTRUCTION), .clk(CLOCK), .Q({imm, INSTRUCTION_AfterReg[19:15], funct3, INSTRUCTION_AfterReg[11:0]}));  // open: en, clr
  Register #(.width(32)) PC (.D(adder_1_out), .clk(CLOCK), .Q(PROGRAM_COUNTER));  // open: en, clr
  imm_gen imm_gen_1 (
    .ImmSel(3'b111), .inst({imm, INSTRUCTION_AfterReg[19:15], funct3, INSTRUCTION_AfterReg[11:0]}),
    .imm(immediate));
  Register #(.width(32)) register_2 (.D(PROGRAM_COUNTER), .clk(CLOCK), .Q(PC_AfterReg));  // open: en, clr
  regfile_main RegFile (
    .rd(INSTRUCTION_AfterReg[11:7]), .Read_Data_1(rs1_output), .ra(ra), .sp(sp), .t0(t0), .t1(t1), .t2(t2),
    .s0(s0), .s1(s1), .a0(a0), .rs1(INSTRUCTION_AfterReg[19:15]), .Write_Data(WBValue), .RegWEn(1'b1),
    .clk(CLOCK));  // open: rs2, Read_Data_2, out_19, out_20, in_7, in_8
  // branch_comp branch_comp_1: pin names not known
  alu Arithmetic_Logic_Unit (
    .Result(ALU_output), .A(rs1_output), .B(immediate));  // open: ALUSel, in_4, in_5, out_9, out_10, in_6, in_7, out_11, out_12
  // mem_main DMEM: pin names not known; wires that end beside it: CLOCK, DMEM_ReadData
  Multiplexer #(.select(2), .width(32), .enable("false")) multiplexer_1 (
    .in1(ALU_output), .in2(DMEM_ReadData), .out(WBValue), .sel(2'b01));  // open: in0, in3

  // Other names for the same wires on the sheet: clk = CLOCK; opcode[6:0] = INSTRUCTION_AfterReg[6:0];
  //   rd[4:0] = INSTRUCTION_AfterReg[11:7]; INSTRUCTION_AfterReg (some bits) = {imm, funct3};
  //   rs1_input[4:0] = INSTRUCTION_AfterReg[19:15]

  // Notes on the sheet:
  //   Output
  //   IMEM (do **NOT** move this)
  //   Inputs
  //   It is OK to move the PC, RegFile, ALU, MEM, Branch Comp, Imm Gen, and Control Logic to wherever is most convenient for you when constructing your CPU, and to delete this text
  //   Inputs/Outputs for testing. Do **NOT** move these.
endmodule
